// Digital circuit lab03.dig as structural Verilog
module lab03 (
  input  [31:0] instruction,
  input  [31:0] A,
  input  [31:0] B,
  output reg__dst,
  output branch,
  output mem__read,
  output mem__to__reg,
  output mem__write,
  output alu__src,
  output reg__write,
  output zero,
  output [31:0] result,
  output [1:0] alu__op
);

  wire [3:0] u_alu_control_alu_control;

  control #(.applicationType("IVERILOG"), .CodeFile("\\workspaces\\Lab03-DatapathControlUnit\\control.v")) u_control (
    .instr_op(instruction[31:26]), .reg_dst(reg__dst), .branch(branch), .mem_read(mem__read),
    .mem_to_reg(mem__to__reg), .alu_op(alu__op), .mem_write(mem__write), .alu_src(alu__src),
    .reg_write(reg__write));
  alu_control #(.applicationType("IVERILOG"), .CodeFile("\\workspaces\\Lab03-DatapathControlUnit\\alu_control.v")) u_alu_control (
    .alu_op(alu__op), .funct(instruction[5:0]), .alu_control(u_alu_control_alu_control));
  alu #(.applicationType("IVERILOG"), .CodeFile("\\workspaces\\Lab03-DatapathControlUnit\\alu.v")) u_alu (
    .alu_control(u_alu_control_alu_control), .A(A), .B(B), .zero(zero), .result(result));

  // Other names for the same wires on the sheet: instr__5__0[5:0] = instruction[5:0]
endmodule

/* Test case Lab 03 Test Bench:
instruction A          B        zero     result     reg\_dst branch mem\_read mem\_to\_reg alu\_op mem\_write alu\_src reg\_write
0x00000024  0xFFFFFFFF 0x0001   0        0x0001     1        0      0         0            10      0          0        1
0x00000025  0xFFFFFFFF 0x0001   0        0xFFFFFFFF 1        0      0         0            10      0          0        1
0x00000020  0xFFFFFFFF 0x0001   1        0x0000     1        0      0         0            10      0          0        1
0x00000022  0xFFFFFFFF 0x0001   0        0xFFFFFFFE 1        0      0         0            10      0          0        1
0x0000002A  0xFFFFFFFF 0x0001   0        0x0001     1        0      0         0            10      0          0        1
0x00000027  0xFFFFFFFF 0x0001   1        0x0000     1        0      0         0            10      0          0        1
0x20000004  0xfffffffb 0x0004   0        0xffffffff 0        0      0         0            00      0          1        1
0x8C000020  0x000000FF 0x0020   0        0x011F     0        0      1         1            00      0          1        1
0xAC000064  0x000000FF 0x0064   0        0x0163     0        0      0         0            00      1          1        0
0x10000025  0x000000FF 0x0025   0        0x00DA     X        1      0         0            01      0          0        0
0x20000004  0xfffffffb 0x0004   0        0xffffffff 0        0      0         0            00      0          1        1
*/
